# Fritzing sketch DiagramaDeConexiones (saved by Fritzing 0.9.9b)
breadboards: 1

parts:
  Componente1 = Arduino Uno (Rev3)
  Componente2 = Thumb Joystick
  R1 = Rotary Potentiometer (Small) [maximum_resistance=100kΩ package=THT]
  R2 = Rotary Potentiometer (Small) [maximum_resistance=100kΩ package=THT]
  HC-SR04_Sensor_1 = HC-SR04 Ultrasonic Distance Sensor

nets:
  N1: Componente1.A0, Componente2.VERT
  N2: Componente1.A1, Componente2.HORZ
  N3: Componente1.A3, R1.wiper
  N4: Componente1.A4/SDA, R2.wiper
  N5: Componente1.D2, Componente2.SEL
  N6: Componente1.D3_PWM, HC-SR04_Sensor_1.ECHO
  N7: Componente1.D4, HC-SR04_Sensor_1.TRIG
  VCC: Componente1.5V, Componente2.VCC, R1.leg1, R2.leg1, HC-SR04_Sensor_1.VCC
  GND: Componente1.GND, Componente2.GND, R1.leg2, R2.leg2, HC-SR04_Sensor_1.GND
